// Logisim project ALU.circ as structural Verilog: 1 circuit, main circuit main
module main (
  input  [31:0] A,
  input  [31:0] in_2,
  input  [31:0] B,
  input  [3:0] OPERATION,
  output PF,
  output ZF,
  output NF,
  output EQUAL
);

  wire comparator_1_lt, comparator_2_lt;
  wire [31:0] ADD, AND, HI_DIV, HI_MUL, LO_DIVU, LO_MUL, NOR, OR, S_LESS, SUB, U_LESS, undriven, undriven_2,
       XOR;

  Multiplier #(.width(32)) multiplier_1 (.a(A), .b(B), .out(LO_MUL), .cout(HI_MUL));  // open: cin
  Divider #(.width(32)) divider_1 (.a(A), .b(B), .out(LO_DIVU), .rem(HI_DIV));  // open: upper
  Adder #(.width(32)) adder_1 (.a(A), .b(B), .out(ADD));  // open: cin, cout
  Subtractor #(.width(32)) subtractor_1 (.a(A), .b(B), .out(SUB));  // open: bin, bout
  Comparator #(.width(32)) comparator_1 (.a(A), .b(B), .eq(EQUAL), .lt(comparator_1_lt));  // open: gt
  assign S_LESS = {{31{1'b0}}, comparator_1_lt};  // Bit_Extender bit_extender_1
  Comparator #(.width(32)) comparator_2 (.a(A), .b(B), .lt(comparator_2_lt));  // open: gt, eq
  assign U_LESS = {{31{1'b0}}, comparator_2_lt};  // Bit_Extender bit_extender_2
  assign AND = A & B;  // AND_Gate and_1, 32 bits wide
  assign OR = A | B;  // OR_Gate or_1, 32 bits wide
  assign XOR = A ^ B;  // XOR_Gate xor_1, 32 bits wide
  assign NOR = ~(A | B);  // NOR_Gate nor_1, 32 bits wide
  Multiplexer #(.select(4), .width(32), .disabled(0), .enable("false")) multiplexer_1 (
    .in0({32{1'b0}}), .in1(A), .in2(S_LESS), .in3(U_LESS), .in4(LO_MUL), .in5(undriven), .in6(undriven_2),
    .in7(LO_DIVU), .in8(ADD), .in9(SUB), .in10(AND), .in11(OR), .in12(NOR), .in13(XOR), .out(in_2),
    .sel(OPERATION));  // open: in14, in15
  Comparator #(.width(32)) comparator_3 (.a(in_2), .b({32{1'b0}}), .gt(PF), .eq(ZF), .lt(NF));

  // Other names for the same wires on the sheet: OP[3:0] = OPERATION
endmodule
